# Fritzing sketch Devre (saved by Fritzing 0.9.3b)

parts:
  Arduino_UNO = Arduino Uno (Rev3)
  VCC1 = Battery
  VCC2 = Battery
  VCC3 = Battery
  VCC4 = Battery
  S1 = H-Bridge with L298N
  LCD2 = LCD screen
  LCM1602_IIC2 = LCM1602 IIC [part_number="LCM1602 IIC" chip_label="LCM1602 IIC" package="DIP (Dual Inline) [THT]"]
  Parça1 = Bluetooth HC-05 Macho
  M1 = DC Motor
  M2 = DC Motor
  M3 = DC Motor
  M4 = DC Motor

nets:
  N1: Arduino_UNO.D8, Parça1.RXD
  N2: Arduino_UNO.D9_PWM, Parça1.TXD
  GND: Arduino_UNO.GND, VCC4.-, S1.GND, LCM1602_IIC2.GND
  N3: Arduino_UNO.A4/SDA, LCM1602_IIC2.SCL
  N4: Arduino_UNO.A5/SCL, LCM1602_IIC2.SDA
  N5: Arduino_UNO.D2, S1.IN4
  N6: Arduino_UNO.D3_PWM, S1.ENB
  N7: Arduino_UNO.D4, S1.IN3
  N8: Arduino_UNO.D5_PWM, S1.ENA
  N9: Arduino_UNO.D6_PWM, S1.IN1
  N10: Arduino_UNO.D7, S1.IN2
  5V: Arduino_UNO.5V, LCM1602_IIC2.VCC
  N11: VCC1.-, VCC2.+
  N12: VCC1.+, S1.12V
  N13: VCC2.-, VCC3.+
  N14: VCC3.-, VCC4.+
  N15: S1.M1-01, M3.pin_1, M4.pin_1
  N16: S1.M1-02, M4.pin_2
  N17: S1.M2-01, M2.pin_2
  N18: S1.M2-02, M1.pin_1
  VSS: LCD2.VSS, LCM1602_IIC2.VSS
  VDD: LCD2.VDD, LCM1602_IIC2.VDD
  N19: LCD2.V0, LCM1602_IIC2.V0
  N20: LCD2.RS, LCM1602_IIC2.RS
  N21: LCD2.R/W, LCM1602_IIC2.RW
  N22: LCD2.E, LCM1602_IIC2.E
  N23: LCD2.DB0, LCM1602_IIC2.D0
  N24: LCD2.DB1, LCM1602_IIC2.D1
  N25: LCD2.DB2, LCM1602_IIC2.D2
  N26: LCD2.DB3, LCM1602_IIC2.D3
  N27: LCD2.DB4, LCM1602_IIC2.D4
  N28: LCD2.DB5, LCM1602_IIC2.D5
  N29: LCD2.DB6, LCM1602_IIC2.D6
  N30: LCD2.DB7, LCM1602_IIC2.D7
  N31: LCD2.LED+, LCM1602_IIC2.A
  N32: LCD2.LED-, LCM1602_IIC2.K
  N33: LCM1602_IIC2.LED_A, LCM1602_IIC2.LED_B

custom parts:
  H-Bridge with L298N: h-bridge
  LCM1602 IIC: I2C-Module to use a 1602 or 2004 LCD on with the wire.h libory Serial LCD Modul
